# Fritzing sketch ElectricalDiagram (saved by Fritzing 1.0.2b)
circuit board: 8.46667cm x 5.64444cm
breadboards: 1

parts:
  Teensy1 = Teensy 4.1
  CUI-enc1 = AMT103
  CUI-enc2 = AMT103
  CUI-enc3 = AMT103
  CUI-enc4 = AMT103
  CUI-enc5 = AMT103
  CUI-enc6 = AMT103
  S1 = D2F-FL Omron Snap Action Limit Switch with Level
  S2 = D2F-FL Omron Snap Action Limit Switch with Level
  S3 = D2F-FL Omron Snap Action Limit Switch with Level
  S4 = D2F-FL Omron Snap Action Limit Switch with Level
  S5 = D2F-FL Omron Snap Action Limit Switch with Level
  S6 = D2F-FL Omron Snap Action Limit Switch with Level
  M1 = Stepper Motor - Bipolar
  M2 = Stepper Motor - Bipolar
  M3 = Stepper Motor - Bipolar
  M4 = Stepper Motor - Bipolar
  M5 = Stepper Motor - Bipolar
  M6 = Stepper Motor - Bipolar
  A1 = DM860A Stepper Motor Driver
  A2 = DM860A Stepper Motor Driver
  A3 = DM860A Stepper Motor Driver
  A4 = DM860A Stepper Motor Driver
  A5 = DM860A Stepper Motor Driver
  A6 = DM860A Stepper Motor Driver
  A7 = S-350-60 Power Supply [part_number=S-350-60 package=THT]
  EVB-LAN9252-SPI1 = EVB-LAN9252-SPI [part_number=EVB-LAN9252-SPI]

nets:
  N1: Teensy1.GND, Teensy1.GND2#55
  N2: Teensy1.D0, A1.PUL-(PUL)
  N3: Teensy1.D1, A1.DIR-(DIR)
  N4: Teensy1.D2, A2.PUL-(PUL)
  N5: Teensy1.D3, A2.DIR-(DIR)
  N6: Teensy1.D4, A3.PUL-(PUL)
  N7: Teensy1.D5, A3.DIR-(DIR)
  N8: Teensy1.D6, A4.PUL-(PUL)
  N9: Teensy1.D7, A4.DIR-(DIR)
  N10: Teensy1.D8, A5.PUL-(PUL)
  N11: Teensy1.D9, A5.DIR-(DIR)
  N12: Teensy1.D10, EVB-LAN9252-SPI1.CS
  N13: Teensy1.D11, EVB-LAN9252-SPI1.MOSI
  N14: Teensy1.D12, EVB-LAN9252-SPI1.MISO
  N15: Teensy1.D13, EVB-LAN9252-SPI1.SCK
  N16: Teensy1.A0/D14, CUI-enc1.A
  N17: Teensy1.A1/D15, CUI-enc1.B
  N18: Teensy1.A6/D20, CUI-enc4.A
  N19: Teensy1.A7/D21, CUI-enc4.B
  N20: Teensy1.A8/D22, CUI-enc5.A
  N21: Teensy1.A9/D23, CUI-enc5.B
  N22: Teensy1.3V3_LOW, S1.Pin_2, S2.Pin_2, S3.Pin_2, S4.Pin_2, S5.Pin_2, S6.Pin_2, EVB-LAN9252-SPI1.3V3
  GND: Teensy1.GND2#31, CUI-enc1.GND, CUI-enc2.GND, CUI-enc3.GND, CUI-enc4.GND, CUI-enc5.GND, CUI-enc6.GND, S1.Pin_3, S2.Pin_3, S3.Pin_3, S4.Pin_3, S5.Pin_3, S6.Pin_3, A1.ENBL-(ENB), A2.ENBL-(ENB), A3.ENBL-(ENB), A4.ENBL-(ENB), A5.ENBL-(ENB), A6.ENBL-(ENB), EVB-LAN9252-SPI1.GND
  5V: Teensy1.Vin, CUI-enc1.5V, CUI-enc2.5V, CUI-enc3.5V, CUI-enc4.5V, CUI-enc5.5V, CUI-enc6.5V, A1.ENBL+(+5V), A1.DIR+(+5V), A1.PUL+(+5V), A2.ENBL+(+5V), A2.DIR+(+5V), A2.PUL+(+5V), A3.ENBL+(+5V), A3.DIR+(+5V), A3.PUL+(+5V), A4.ENBL+(+5V), A4.DIR+(+5V), A4.PUL+(+5V), A5.ENBL+(+5V), A5.DIR+(+5V), A5.PUL+(+5V), A6.ENBL+(+5V), A6.DIR+(+5V), A6.PUL+(+5V)
  N23: Teensy1.A10/D24, CUI-enc6.A
  N24: Teensy1.A11/D25, CUI-enc6.B
  N25: Teensy1.A12/D26, S1.Pin_1
  N26: Teensy1.A13/D27, S2.Pin_1
  N27: Teensy1.D28, S3.Pin_1
  N28: Teensy1.D29, S4.Pin_1
  N29: Teensy1.D30, S5.Pin_1
  N30: Teensy1.D31, S6.Pin_1
  N31: Teensy1.D33, A6.PUL-(PUL)
  N32: Teensy1.D34, A6.DIR-(DIR)
  N33: Teensy1.D36, CUI-enc3.A
  N34: Teensy1.D37, CUI-enc3.B
  N35: Teensy1.A14/D38, CUI-enc2.A
  N36: Teensy1.A15/D39, CUI-enc2.B
  N37: M1.A, A1.A+
  N38: M1.C, A1.A-
  N39: M1.B, A1.B+
  N40: M1.D, A1.B-
  N41: M2.A, A2.A+
  N42: M2.C, A2.A-
  N43: M2.B, A2.B+
  N44: M2.D, A2.B-
  N45: M3.A, A3.A+
  N46: M3.C, A3.A-
  N47: M3.B, A3.B+
  N48: M3.D, A3.B-
  N49: M4.A, A4.A+
  N50: M4.C, A4.A-
  N51: M4.B, A4.B+
  N52: M4.D, A4.B-
  N53: M5.A, A5.A+
  N54: M5.C, A5.A-
  N55: M5.B, A5.B+
  N56: M5.D, A5.B-
  N57: M6.A, A6.A+
  N58: M6.C, A6.A-
  N59: M6.B, A6.B+
  N60: M6.D, A6.B-
  N61: A1.VDC, A2.VDC, A3.VDC, A4.VDC, A5.VDC, A6.VDC, A7.+V1, A7.+V3
  GND_2: A1.GND, A2.GND, A3.GND, A4.GND, A5.GND, A6.GND, A7.-V1, A7.-V3

custom parts:
  Teensy 4.1: The Teensy is a complete USB-based microcontoller development system, in a very small footprint, capable of implementing many types of projects. All programming is done via the USB port. No special programmer is needed, only a standard micro-USB cable and a PC or Macintosh with a USB port.
  D2F-FL Omron Snap Action Limit Switch with Level: Snap action switch with stainless steel lever.
  DM860A Stepper Motor Driver: DM860A is a type of two-phase hybrid stepping motor driver, The drive voltage of which is from 24VDC to 80VDC. It is designed for use with 2-phase hybrid stepper motor of all kinds with 57mm to 110mm outside diameter and less than 8.0A phase current. Mar 2023: Correct pcb layerId as the part won't save correctly in a .fzz file as is.
  S-350-60 Power Supply: 350W Stepper motor power supply. June 2024 clean up errors in the part.
